# Fritzing sketch shema (saved by Fritzing 0.9.3b)
breadboards: 1

parts:
  Button = Pushbutton [package="[SMD]"]
  Potentiometer = Rotary Potentiometer (Small) [maximum_resistance=100kΩ package=THT]
  RGB_LED = RGB LED (com. cathode, rgb) [package="5 mm [THT]"]
  Arduino = Arduino Nano (Rev3.0)

nets:
  N1: Button.Pin_1, Button.Pin_2, Potentiometer.leg2, Arduino.5V
  N2: Button.Pin_3, Button.Pin_4, Arduino.D9
  N3: Potentiometer.leg1, RGB_LED.common_cathode, Arduino.GND
  N4: Potentiometer.wiper, Arduino.A0
  N5: RGB_LED.red_anode, Arduino.D6
  N6: RGB_LED.green_anode, Arduino.D7
  N7: RGB_LED.blue_anode, Arduino.D8
